# Fritzing sketch Untitled Sketch (saved by Fritzing 0.9.0b)

parts:
  元件1 = Arduino Pro Mini v13
  U1 = LCD-16X2 [package=lcd-8x2-kit]
  U2 = 74HC595 [package="DIP16 [THT]"]
  LED17 = smd LED [color="Red (633nm)" package="0805 [SMD]"]
  U3 = 74HC595 [package="DIP16 [THT]"]
  R1 = Resistor [tolerance=±5% resistance=220 package=THT]
  U4 = 74HC595 [package="DIP16 [THT]"]
  LED1 = LED - 5mm [color="Red (633nm)" package="5 mm [THT]"]
  LED2 = LED - 5mm [color="Red (633nm)" package="5 mm [THT]"]
  LED3 = LED - 5mm [color="Red (633nm)" package="5 mm [THT]"]
  LED4 = LED - 5mm [color="Red (633nm)" package="5 mm [THT]"]
  LED5 = LED - 5mm [color="Red (633nm)" package="5 mm [THT]"]
  LED6 = LED - 5mm [color="Red (633nm)" package="5 mm [THT]"]
  LED7 = LED - 5mm [color="Red (633nm)" package="5 mm [THT]"]
  LED8 = LED - 5mm [color="Red (633nm)" package="5 mm [THT]"]
  R2 = Resistor [tolerance=±5% resistance=220 package=THT]
  R3 = Resistor [tolerance=±5% resistance=220 package=THT]
  R6 = Resistor [tolerance=±5% resistance=220 package=THT]
  R7 = Resistor [tolerance=±5% resistance=220 package=THT]
  R8 = Resistor [tolerance=±5% resistance=220 package=THT]
  R9 = Resistor [tolerance=±5% resistance=220 package=THT]
  R10 = Resistor [tolerance=±5% resistance=220 package=THT]
  R11 = Resistor [tolerance=±5% resistance=220 package=THT]
  LED9 = LED - 5mm [color="Red (633nm)" package="5 mm [THT]"]
  LED10 = LED - 5mm [color="Red (633nm)" package="5 mm [THT]"]
  LED11 = LED - 5mm [color="Red (633nm)" package="5 mm [THT]"]
  LED12 = LED - 5mm [color="Red (633nm)" package="5 mm [THT]"]
  LED13 = LED - 5mm [color="Red (633nm)" package="5 mm [THT]"]
  LED14 = LED - 5mm [color="Red (633nm)" package="5 mm [THT]"]
  LED15 = LED - 5mm [color="Red (633nm)" package="5 mm [THT]"]
  LED16 = LED - 5mm [color="Red (633nm)" package="5 mm [THT]"]
  R12 = Resistor [tolerance=±5% resistance=220 package=THT]
  R13 = Resistor [tolerance=±5% resistance=220 package=THT]
  R14 = Resistor [tolerance=±5% resistance=220 package=THT]
  R15 = Resistor [tolerance=±5% resistance=220 package=THT]
  R16 = Resistor [tolerance=±5% resistance=220 package=THT]
  R17 = Resistor [tolerance=±5% resistance=220 package=THT]
  R18 = Resistor [tolerance=±5% resistance=220 package=THT]
  R19 = Resistor [tolerance=±5% resistance=220 package=THT]
  S12 = Pushbutton [package=THT]
  R30 = Resistor [tolerance=±5% resistance=10k package=THT]
  S2 = Pushbutton [package=THT]
  R21 = Resistor [tolerance=±5% resistance=10k package=THT]
  S3 = Pushbutton [package=THT]
  R22 = Resistor [tolerance=±5% resistance=10k package=THT]
  S5 = Pushbutton [package=THT]
  S6 = Pushbutton [package=THT]
  S7 = Pushbutton [package=THT]
  R24 = Resistor [tolerance=±5% resistance=10k package=THT]
  R25 = Resistor [tolerance=±5% resistance=10k package=THT]
  R26 = Resistor [tolerance=±5% resistance=10k package=THT]
  S9 = Pushbutton [package=THT]
  S11 = Pushbutton [package=THT]
  R28 = Resistor [tolerance=±5% resistance=10k package=THT]
  R29 = Resistor [tolerance=±5% resistance=10k package=THT]
  U5 = JOYSTICK-PSP1000 [package=joystick-psp1000]
  U6 = JOYSTICK-PSP1000 [package=joystick-psp1000]

nets:
  5V/VCC/Vdd: 元件1.VCC, U1.VDD, U2.MR, U2.VCC, LED17.anode, U3.MR, U3.VCC, U4.MR, U4.VCC, S12.leg0, S2.leg0, S3.leg0, S5.leg0, S6.leg0, S7.leg0, S9.leg0, S11.leg0, U5.VCC, U6.VCC
  GND/Vss: 元件1.GND, U1.VSS, U1.R_W, U1.K, U2.GND, U2.OE, U3.GND, U3.OE, R1.Pin_1, U4.GND, U4.OE, R2.Pin_1, R3.Pin_1, R6.Pin_1, R7.Pin_1, R8.Pin_1, R9.Pin_1, R10.Pin_1, R11.Pin_1, R12.Pin_1, R13.Pin_1, R14.Pin_1, R15.Pin_1, R16.Pin_1, R17.Pin_1, R18.Pin_1, R19.Pin_1, R30.Pin_1, R21.Pin_1, R22.Pin_1, R24.Pin_1, R25.Pin_1, R26.Pin_1, R28.Pin_1, R29.Pin_1, U5.GND, U6.GND
  N1: 元件1.A3, U6.Y
  N2: 元件1.A2, U6.X
  N3: 元件1.A1, U5.Y
  N4: 元件1.A0, U5.X
  SCK: 元件1.D13/SCK
  MISO: 元件1.D12/MISO
  MOSI: 元件1.D11_PWM/MOSI
  CE: 元件1.D10_PWM/SS
  CSN: 元件1.D9_PWM
  Q8: 元件1.D7
  SERIAL CONTROL: 元件1.D6_PWM
  N5: 元件1.D5_PWM, U3.ST_CP
  N6: 元件1.D4, U1.E, U2.ST_CP
  N7: 元件1.D3_PWM, U2.DS, U3.DS, U4.DS
  CLOCK: 元件1.D2, U2.SH_CP, U3.SH_CP, U4.SH_CP
  N8: U1.VO, R1.Pin_0
  N9: U1.RS, U2.Q2
  N10: U1.DB4, U2.Q3
  N11: U1.DB5, U2.Q4
  N12: U1.DB6, U2.Q5
  N13: U1.DB7, U2.Q6
  N14: U1.A, LED17.cathode
  N15: U3.Q1, LED8.anode
  N16: U3.Q2, LED6.anode
  N17: U3.Q3, LED7.anode
  N18: U3.Q4, LED4.anode
  N19: U3.Q5, LED3.anode
  N20: U3.Q6, LED2.anode
  N21: U3.Q7, LED1.anode
  N22: U3.Q7', U4.ST_CP
  N23: U3.Q0, LED5.anode
  N24: U4.Q1, LED9.anode
  N25: U4.Q2, LED12.anode
  N26: U4.Q3, LED16.anode
  N27: U4.Q4, LED10.anode
  N28: U4.Q5, LED15.anode
  N29: U4.Q6, LED13.anode
  N30: U4.Q7, LED11.anode
  N31: U4.Q0, LED14.anode
  N32: LED1.cathode, R2.Pin_0
  N33: LED2.cathode, R3.Pin_0
  N34: LED3.cathode, R6.Pin_0
  N35: LED4.cathode, R7.Pin_0
  N36: LED5.cathode, R10.Pin_0
  N37: LED6.cathode, R8.Pin_0
  N38: LED7.cathode, R9.Pin_0
  N39: LED8.cathode, R11.Pin_0
  N40: LED9.cathode, R13.Pin_0
  N41: LED10.cathode, R16.Pin_0
  N42: LED11.cathode, R14.Pin_0
  N43: LED12.cathode, R12.Pin_0
  N44: LED13.cathode, R18.Pin_0
  N45: LED14.cathode, R15.Pin_0
  N46: LED15.cathode, R17.Pin_0
  N47: LED16.cathode, R19.Pin_0
  P1-1: S12.leg1, R30.Pin_0
  P1-2: S2.leg1, R21.Pin_0
  P1-3: S3.leg1, R22.Pin_0
  P1-4: S5.leg1, R24.Pin_0
  P1-6: S6.leg1, R26.Pin_0
  P1-5: S7.leg1, R25.Pin_0
  P1-7: S9.leg1, R28.Pin_0
  1.P1-8: S11.leg1, R29.Pin_0
